# Fritzing sketch 1DigitSetup (saved by Fritzing 1.0.1rc)
breadboards: 1

parts:
  R1 = Resistor [tolerance=±5% resistance=220 package="2512 [SMD]"]
  U1 = 7-SEGMENT-DISPLAY [package=7-segment-display]
  Part2 = Arduino Uno (Rev3) - ICSP

nets:
  N1: R1.Pin_0, U1.C
  N2: R1.Pin_1, Part2.D2
  N3: U1.E, Part2.D12/MISO
  N4: U1.D, Part2.D10_PWM/SS
  N5: U1.G1, Part2.D9_PWM
  N6: U1.DP, Part2.D13/SCK
  N7: U1.B, Part2.D8
  N8: U1.A, Part2.D7
  N9: U1.G2, Part2.D6_PWM
  N10: U1.G, Part2.ICSP_MOSI, Part2.D11_PWM/MOSI
