# Fritzing sketch single7 (saved by Fritzing 1.0.1rc)
breadboards: 1

parts:
  Part1 = Arduino ProtoShield
  DI1 = 7-Segment LED Display [package=THT]
  R1 = Resistor [tolerance=±5% resistance=220 package="2512 [SMD]"]

nets:
  N1: Part1.D2, R1.Pin_1
  N2: Part1.D6, DI1.cathodeA
  N3: Part1.D7, DI1.cathodeB
  N4: DI1.commAnode#2, R1.Pin_0
